# Fritzing sketch mosfet_dcmotor (saved by Fritzing 0.9.1b)
breadboards: 1

parts:
  Q1 = Basic FET N-Channel [part_number=IRL540 package="TO220 [THT]"]
  R1 = Resistor [tolerance=±5% resistance=100 package=THT]
  R2 = Resistor [tolerance=±5% resistance=22k package=THT]
  Power_plug1 = Power plug [part_number="12V DC"]
  Part1 = Arduino Nano (Rev3.0) (ICSP)
  D1 = Diode [part_number=1N4001 package=diode-1n4001]
  M1 = DC Motor

nets:
  N1: Q1.gate, R1.Pin_0, R2.Pin_0
  N2: Q1.drain, D1.A, M1.pin_2
  GND: Q1.source, R2.Pin_1, Power_plug1.GND, Part1.GND
  N3: R1.Pin_1, Part1.D9
  VCC: Power_plug1.VCC, Part1.VIN, D1.C, M1.pin_1
